// Digital circuit MC14500_Clone_logic_2.dig as structural Verilog
module MC14500_Clone_logic_2 (
  input  Din,
  input  I0,
  input  I1,
  input  I2,
  input  I3,
  input  nRST,
  input  clk,
  output Dout,
  output WR
);

  wire _7474_1_pin6, _7474_2_pin9, _7474_2_pin11, _74138_1_pin4, _74151_1_pin1, _74151_1_pin4,
       _74151_1_pin12, _74151_1_pin13, and_1_out, FLAG_F, JMP, nand_1_out, nand_2_out, nand_3_out,
       nand_4_out, nD, nIEN, nJMP, nNOPF, nOEN, not_1_out, not_2_out, nQ, nRTN, nSKZ, nSTO, nSTOC, or_1_out,
       or_2_out, Q, RR, RTN, xor_1_out, xor_3_out;

  not not_1 (not_1_out, I0);
  _74138 _74138_1 (
    .pin1(I0), .pin2(I1), .pin3(I2), .pin4(_74138_1_pin4), .pin5(_74138_1_pin4), .pin6(I3), .pin7(nNOPF),
    .pin8(1'b0), .pin9(nSKZ), .pin10(nRTN), .pin11(nJMP), .pin12(nOEN), .pin13(nIEN), .pin14(nSTOC),
    .pin15(nSTO), .pin16(1'b1));
  xor xor_1 (xor_1_out, Din, not_1_out);
  or or_1 (or_1_out, _74151_1_pin4, nSKZ);
  _7474 _7474_1 (
    .pin1(1'b1), .pin2(Din), .pin3(nIEN), .pin4(nRST), .pin6(_7474_1_pin6), .pin7(1'b0), .pin9(RR),
    .pin10(nRST), .pin11(nOEN), .pin12(Din), .pin13(1'b1), .pin14(1'b1));  // open: pin5, pin8
  and and_1 (and_1_out, or_1_out, nRTN);
  not not_2 (not_2_out, and_1_out);
  or or_2 (or_2_out, not_2_out, clk);
  _74151 _74151_1 (
    .pin1(_74151_1_pin1), .pin2(xor_1_out), .pin3(xor_1_out), .pin4(_74151_1_pin4), .pin5(Q), .pin6(nQ),
    .pin7(_7474_1_pin6), .pin8(1'b0), .pin9(I2), .pin10(I1), .pin11(I0), .pin12(_74151_1_pin12),
    .pin13(_74151_1_pin13), .pin14(_74151_1_pin13), .pin15(_74151_1_pin1), .pin16(1'b1));
  nand nand_1 (nand_1_out, and_1_out, nand_2_out);
  nand nand_2 (nand_2_out, nand_1_out, or_2_out);
  nand nand_3 (nand_3_out, nSTOC, nSTO);
  and and_2 (WR, nand_3_out, RR);
  xor xor_2 (_74151_1_pin12, xor_3_out, 1'b1);
  _7474 _7474_2 (
    .pin1(1'b1), .pin2(nand_2_out), .pin3(clk), .pin4(nRST), .pin6(_74138_1_pin4), .pin7(1'b0),
    .pin8(_74151_1_pin4), .pin9(_7474_2_pin9), .pin10(nRST), .pin11(_7474_2_pin11), .pin12(Q), .pin13(1'b1),
    .pin14(1'b1));  // open: pin5
  nand nand_4 (nand_4_out, nD, clk);
  and and_3 (_74151_1_pin1, _74151_1_pin4, xor_1_out);
  or or_3 (_74151_1_pin13, _74151_1_pin4, xor_1_out);
  xor xor_3 (xor_3_out, _74151_1_pin4, xor_1_out);
  or or_4 (_7474_2_pin11, _74138_1_pin4, nand_4_out);
  not not_3 (JMP, nJMP);
  not not_4 (RTN, nRTN);
  not not_5 (FLAG_F, nNOPF);
  not not_6 (nD, I3);
  xor xor_4 (Dout, nSTO, _7474_2_pin9);
  LED NOPF (.in(nNOPF));
  LED NOP0 (.in(nSTO));
  LED Fout (.in(RR));
  LED u_Din (.in(Din));
  LED led_1 (.in(nQ));
  LED led_2 (.in(Q));

  // Other names for the same wires on the sheet: A = I0; B = I1; C = I2; D = I3

  // Notes on the sheet:
  //   MC14500 CLONE
endmodule
